// Logisim project ex5.circ as structural Verilog: 5 circuits, main circuit rotr
module rotr (
  input  [15:0] A,
  input  [3:0] B,
  output [15:0] Out1
);

  wire [15:0] adder_1_out, adder_2_out, adder_3_out, demultiplexer_1_out0, demultiplexer_1_out1,
       demultiplexer_2_out0, demultiplexer_2_out1, demultiplexer_3_out0, demultiplexer_3_out1,
       demultiplexer_4_out0, demultiplexer_4_out1, rot1_1_out_2, rot2_1_out_2, rot4_1_out_2, rot8_1_out_2;

  Demultiplexer #(.enable("false"), .width(16)) demultiplexer_1 (
    .out0(demultiplexer_1_out0), .out1(demultiplexer_1_out1), .in(A), .sel(B[0]));
  rot1 rot1_1 (.in_1(demultiplexer_1_out1), .out_2(rot1_1_out_2));
  Demultiplexer #(.enable("false"), .width(16)) demultiplexer_2 (
    .out0(demultiplexer_2_out0), .out1(demultiplexer_2_out1), .in(adder_1_out), .sel(B[1]));
  Adder #(.width(16)) adder_1 (.a(demultiplexer_1_out0), .b(rot1_1_out_2), .out(adder_1_out));  // open: cin, cout
  rot2 rot2_1 (.in_1(demultiplexer_2_out1), .out_2(rot2_1_out_2));
  Demultiplexer #(.enable("false"), .width(16)) demultiplexer_3 (
    .out0(demultiplexer_3_out0), .out1(demultiplexer_3_out1), .in(adder_2_out), .sel(B[2]));
  Adder #(.width(16)) adder_2 (.a(demultiplexer_2_out0), .b(rot2_1_out_2), .out(adder_2_out));  // open: cin, cout
  rot4 rot4_1 (.in_1(demultiplexer_3_out1), .out_2(rot4_1_out_2));
  Demultiplexer #(.enable("false"), .width(16)) demultiplexer_4 (
    .out0(demultiplexer_4_out0), .out1(demultiplexer_4_out1), .in(adder_3_out), .sel(B[3]));
  Adder #(.width(16)) adder_3 (.a(demultiplexer_3_out0), .b(rot4_1_out_2), .out(adder_3_out));  // open: cin, cout
  Adder #(.width(16)) adder_4 (.a(demultiplexer_4_out0), .b(rot8_1_out_2), .out(Out1));  // open: cin, cout
  rot8 rot8_1 (.in_1(demultiplexer_4_out1), .out_2(rot8_1_out_2));

  // Notes on the sheet:
  //   PUT CIRCUITRY HERE
endmodule

module rot8 (
  input  [15:0] in_1,
  output [15:0] out_2
);


  assign out_2 = {in_1[7:0], in_1[15:8]};

  // Notes on the sheet:
  //   PUT CIRCUITRY HERE
endmodule

module rot4 (
  input  [15:0] in_1,
  output [15:0] out_2
);


  assign out_2 = {in_1[3:0], in_1[15:4]};

  // Notes on the sheet:
  //   PUT CIRCUITRY HERE
endmodule

module rot2 (
  input  [15:0] in_1,
  output [15:0] out_2
);


  assign out_2 = {in_1[1:0], in_1[15:2]};

  // Notes on the sheet:
  //   PUT CIRCUITRY HERE
endmodule

module rot1 (
  input  [15:0] in_1,
  output [15:0] out_2
);


  assign out_2 = {in_1[0], in_1[15:1]};

  // Notes on the sheet:
  //   PUT CIRCUITRY HERE
endmodule
