// Logisim project alu.circ as structural Verilog: 1 circuit, main circuit alu
module alu (
  input  [31:0] A,
  input  [31:0] B,
  input  [3:0] ALUSel,
  output [31:0] Result
);

  wire [0:0] slt0;
  wire [30:0] subtractor_2_out;
  wire [31:0] add0, and0, mul0, mulh, mulhu, multiplier_1_out, multiplier_3_out, or0, sll0, sra0, srl0, sub,
       undriven, undriven_2, undriven_3, xor0;
  wire [63:0] shifter_4_out, shifter_5_out;

  assign and0 = A & B;  // AND_Gate and_1, 32 bits wide
  Shifter #(.shift("ar"), .width(32)) shifter_1 (.in(A), .\dist (B[4:0]), .out(sra0));
  Multiplier #(.width(64)) multiplier_1 (
    .a({{32{1'b0}}, A}), .b({{32{1'b0}}, B}), .out({mulhu, multiplier_1_out}));  // open: cin, cout
  Multiplexer #(.enable("false"), .select(4), .width(32)) multiplexer_1 (
    .in0(add0), .in1(and0), .in2(or0), .in3(xor0), .in4(srl0), .in5(sra0), .in6(sll0),
    .in7({{31{1'b0}}, slt0[0]}), .in8(undriven_2), .in9(undriven_3), .in10(mul0), .in11(mulhu), .in12(sub),
    .in13(B), .in14(mulh), .in15(undriven), .out(Result), .sel(ALUSel));
  Adder #(.width(32)) adder_1 (.a(A), .b(B), .out(add0));  // open: cin, cout
  Subtractor #(.width(32)) subtractor_1 (.a(A), .b(B), .out(sub));  // open: bin, bout
  assign or0 = A | B;  // OR_Gate or_1, 32 bits wide
  Shifter #(.width(32)) shifter_2 (.in(A), .\dist (B[4:0]), .out(sll0));
  Subtractor #(.width(32)) subtractor_2 (.a(A), .b(B), .out({slt0[0], subtractor_2_out}));  // open: bin, bout
  assign xor0 = A ^ B;  // XOR_Gate xor_1, 32 bits wide
  Shifter #(.shift("lr"), .width(32)) shifter_3 (.in(A), .\dist (B[4:0]), .out(srl0));
  Multiplier #(.width(32)) multiplier_2 (.a(A), .b(B), .out(mul0));  // open: cin, cout
  Shifter #(.shift("ar"), .width(64)) shifter_4 (.in({A, {32{1'b0}}}), .\dist (6'b100000), .out(shifter_4_out));
  Shifter #(.shift("ar"), .width(64)) shifter_5 (.in({B, {32{1'b0}}}), .\dist (6'b100000), .out(shifter_5_out));
  Multiplier #(.mode("twosComplement"), .width(64)) multiplier_3 (
    .a(shifter_4_out), .b(shifter_5_out), .out({mulh, multiplier_3_out}));  // open: cin, cout

  // Other names for the same wires on the sheet: bsel[31:0] = B

  // Notes on the sheet:
  //   INPUTS to your circuit
  //   DON'T CHANGE THE LOCATIONS OF THE INPUTS AND OUTPUTS!
  //   OUTPUT from your circuit
endmodule
