// Logisim project branch_comp.circ as structural Verilog: 1 circuit, main circuit branch_comp
module branch_comp (
  input  [31:0] rs1,
  input  [31:0] rs2,
  input  BrUn,
  output BrEq,
  output BrLt
);

  wire BrLt_same, multiplexer_1_out, or_1_out, subtractor_2_bout;
  wire [30:0] subtractor_1_out;
  wire [31:0] xor_1_out;
  wire [32:0] subtractor_2_out;

  Subtractor #(.width(32)) subtractor_1 (.a(rs1), .b(rs2), .out({BrLt_same, subtractor_1_out}));  // open: bin, bout
  assign xor_1_out = rs1 ^ rs2;  // XOR_Gate xor_1, 32 bits wide
  Subtractor #(.width(33)) subtractor_2 (
    .a({1'b0, rs1}), .b({1'b0, rs2}), .out(subtractor_2_out), .bout(subtractor_2_bout));  // open: bin
  or or_1 (or_1_out, xor_1_out[0], xor_1_out[1], xor_1_out[2], xor_1_out[3], xor_1_out[4], xor_1_out[5], xor_1_out[6], xor_1_out[7], xor_1_out[8], xor_1_out[9], xor_1_out[10], xor_1_out[11], xor_1_out[12], xor_1_out[13], xor_1_out[14], xor_1_out[15], xor_1_out[16], xor_1_out[17], xor_1_out[18], xor_1_out[19], xor_1_out[20], xor_1_out[21], xor_1_out[22], xor_1_out[23], xor_1_out[24], xor_1_out[25], xor_1_out[26], xor_1_out[27], xor_1_out[28], xor_1_out[29], xor_1_out[30], xor_1_out[31]);
  Multiplexer #(.enable("false")) multiplexer_1 (
    .in0(BrLt_same), .in1(rs1[31]), .out(multiplexer_1_out), .sel(xor_1_out[31]));
  not not_1 (BrEq, or_1_out);
  Multiplexer #(.enable("false")) multiplexer_2 (
    .in0(multiplexer_1_out), .in1(subtractor_2_out[32]), .out(BrLt), .sel(BrUn));
  // also tied to VCC on the sheet: subtractor_2_bout

  // Notes on the sheet:
  //   INPUTS to your circuit
  //   DON'T CHANGE THE LOCATIONS OF THE INPUTS AND OUTPUTS!
  //   OUTPUT from your circuit
endmodule
