// Logisim project control_logic.circ as structural Verilog: 1 circuit, main circuit control_logic
module control_logic (
  input  [31:0] inst,
  input  BrEq,
  input  BrLt,
  output PCSel,
  output RegWEn,
  output [2:0] ImmSel,
  output BrUn,
  output ASel,
  output BSel,
  output [3:0] ALUSel,
  output MemRW,
  output [1:0] WBSel,
  output CSRSel,
  output CSRWen,
  output [3:0] WRITE_ENABLE
);

  wire add, addi, and0, and_1_out, and_2_out, and_3_out, and_4_out, and_5_out, and_6_out, and_7_out,
       and_8_out, and_9_out, and_10_out, and_11_out, and_12_out, and_13_out, and_14_out, and_15_out,
       and_16_out, and_17_out, and_18_out, and_19_out, and_20_out, and_21_out, and_22_out, and_23_out,
       and_24_out, and_25_out, and_26_out, and_27_out, and_28_out, and_29_out, and_30_out, and_31_out,
       and_32_out, and_33_out, and_34_out, and_35_out, and_36_out, and_37_out, and_38_out, and_48_out,
       and_49_out, and_50_out, and_51_out, and_52_out, and_53_out, and_54_out, and_55_out, andi, auipc, beq,
       bge, bgeu, blt, bltu, bne, csrw, demultiplexer_2_out0, demultiplexer_2_out1, demultiplexer_2_out5,
       demultiplexer_3_out0, demultiplexer_3_out1, demultiplexer_8_out5, I, jalr, lb0, lh0, lui, lw0, mul,
       mulh0, mulhu, not_1_out, not_2_out, not_3_out, not_4_out, not_5_out, not_6_out, not_7_out, not_8_out,
       not_9_out, not_10_out, not_11_out, not_12_out, not_13_out, not_14_out, not_15_out, not_16_out,
       not_17_out, not_18_out, not_19_out, not_20_out, not_21_out, not_22_out, not_23_out, not_24_out,
       not_25_out, not_26_out, or0, or_1_out, ori, SB, SB_PCsel, sb_t, sh, sll0, slli, slt0, slti, sra0,
       srai, srl0, srli, sub, U, xor0, xori;

  not not_1 (not_1_out, inst[6]);
  not not_2 (not_2_out, inst[6]);
  and and_1 (and_1_out, inst[6], inst[5]);
  not not_3 (not_3_out, inst[4]);
  and and_2 (and_2_out, inst[6], inst[5]);
  and and_3 (and_3_out, inst[6], inst[5]);
  not not_4 (not_4_out, inst[6]);
  not not_5 (not_5_out, inst[6]);
  not not_6 (not_6_out, inst[5]);
  and and_4 (and_4_out, not_1_out, inst[5]);
  not not_7 (not_7_out, inst[4]);
  and and_5 (and_5_out, inst[6], inst[5]);
  not not_8 (not_8_out, inst[4]);
  not not_9 (not_9_out, inst[4]);
  not not_10 (not_10_out, inst[3]);
  not not_11 (not_11_out, inst[3]);
  and and_6 (and_6_out, not_4_out, inst[5]);
  and and_7 (and_7_out, not_5_out, not_6_out);
  not not_12 (not_12_out, inst[3]);
  not not_13 (not_13_out, inst[3]);
  and and_8 (and_8_out, not_2_out, inst[4]);
  not not_14 (not_14_out, inst[3]);
  and and_9 (and_9_out, and_1_out, not_3_out);
  and and_10 (and_10_out, and_2_out, not_9_out);
  and and_11 (and_11_out, and_3_out, inst[4]);
  not not_15 (not_15_out, inst[2]);
  not not_16 (not_16_out, inst[3]);
  not not_17 (not_17_out, inst[2]);
  not not_18 (not_18_out, inst[3]);
  and and_12 (and_12_out, and_4_out, not_7_out);
  not not_19 (not_19_out, inst[2]);
  and and_13 (and_13_out, and_5_out, not_8_out);
  not not_20 (not_20_out, inst[2]);
  buf and_14 (and_14_out, inst[3]);  // AND_Gate
  and and_15 (and_15_out, and_6_out, inst[4]);
  and and_16 (and_16_out, and_8_out, not_14_out);
  and and_17 (and_17_out, and_10_out, not_10_out);
  and and_18 (and_18_out, and_11_out, not_11_out);
  and and_19 (and_19_out, and_15_out, not_16_out);
  and and_20 (and_20_out, and_7_out, not_18_out);
  and and_21 (and_21_out, and_12_out, not_12_out);
  and and_22 (and_22_out, and_13_out, not_13_out);
  and and_23 (and_23_out, and_14_out, inst[2]);
  and and_24 (and_24_out, and_16_out, inst[2]);
  and and_25 (and_25_out, and_17_out, inst[2]);
  and and_26 (and_26_out, and_18_out, not_15_out);
  not not_21 (not_21_out, inst[2]);
  and and_27 (and_27_out, and_21_out, not_19_out);
  and and_28 (and_28_out, and_22_out, not_20_out);
  and and_29 (and_29_out, and_19_out, not_17_out);
  and and_30 (and_30_out, and_20_out, not_21_out);
  and and_31 (and_31_out, and_23_out, inst[1]);
  and and_32 (and_32_out, and_25_out, inst[1]);
  and and_33 (and_33_out, and_26_out, inst[1]);
  and and_34 (and_34_out, and_27_out, inst[1]);
  and and_35 (and_35_out, and_28_out, inst[1]);
  and and_36 (and_36_out, and_24_out, inst[1]);
  and and_37 (and_37_out, and_29_out, inst[1]);
  and and_38 (and_38_out, and_30_out, inst[1]);
  and and_39 (ImmSel[2], and_31_out, inst[0]);
  and and_40 (MemRW, and_34_out, inst[0]);
  and and_41 (SB, and_35_out, inst[0]);
  and and_42 (U, and_36_out, inst[0]);
  and and_43 (jalr, and_32_out, inst[0]);
  and and_44 (CSRWen, and_33_out, inst[0]);
  and and_45 (BSel, and_37_out, inst[0]);
  and and_46 (I, and_38_out, inst[0]);
  Demultiplexer #(.enable("false"), .select(3)) demultiplexer_1 (
    .out1(csrw), .out5(CSRSel), .in(CSRWen), .sel(inst[14:12]));  // open: out0, out2, out3, out4, out6, out7
  Demultiplexer #(.enable("false"), .select(3)) demultiplexer_2 (
    .out0(demultiplexer_2_out0), .out1(demultiplexer_2_out1), .out2(slt0), .out3(mulhu), .out4(xor0),
    .out5(demultiplexer_2_out5), .out6(or0), .out7(and0), .in(BSel), .sel(inst[14:12]));
  Demultiplexer #(.enable("false")) demultiplexer_3 (
    .out0(demultiplexer_3_out0), .out1(demultiplexer_3_out1), .in(I), .sel(inst[4]));
  Demultiplexer #(.enable("false"), .select(3)) demultiplexer_4 (
    .out0(sb_t), .out1(sh), .out2(WRITE_ENABLE[3]), .in(MemRW), .sel(inst[14:12]));  // open: out3, out4, out5, out6, out7
  Demultiplexer #(.enable("false"), .select(3)) demultiplexer_5 (
    .out0(beq), .out1(bne), .out4(blt), .out5(bge), .out6(bltu), .out7(bgeu), .in(SB), .sel(inst[14:12]));  // open: out2, out3
  Demultiplexer #(.enable("false")) demultiplexer_6 (.out0(auipc), .out1(lui), .in(U), .sel(inst[5]));
  Demultiplexer #(.enable("false"), .select(3)) demultiplexer_7 (
    .out0(lb0), .out1(lh0), .out2(lw0), .in(demultiplexer_3_out0), .sel(inst[14:12]));  // open: out3, out4, out5, out6, out7
  Demultiplexer #(.enable("false"), .select(3)) demultiplexer_8 (
    .out0(addi), .out1(slli), .out2(slti), .out4(xori), .out5(demultiplexer_8_out5), .out6(ori), .out7(andi),
    .in(demultiplexer_3_out1), .sel(inst[14:12]));  // open: out3
  Demultiplexer #(.enable("false")) demultiplexer_9 (.out0(add), .out1(mul), .in(demultiplexer_2_out0), .sel(inst[25]));
  Demultiplexer #(.enable("false")) demultiplexer_10 (
    .out0(sll0), .out1(mulh0), .in(demultiplexer_2_out1), .sel(inst[25]));
  Demultiplexer #(.enable("false")) demultiplexer_11 (
    .out0(srl0), .out1(sra0), .in(demultiplexer_2_out5), .sel(inst[30]));
  and and_47 (sub, inst[30], demultiplexer_2_out0);
  Demultiplexer #(.enable("false")) demultiplexer_12 (
    .out0(srli), .out1(srai), .in(demultiplexer_8_out5), .sel(inst[30]));
  not not_22 (not_22_out, BrEq);
  not not_23 (not_23_out, BrLt);
  and and_48 (and_48_out, beq, BrEq);
  and and_49 (and_49_out, blt, BrLt);
  and and_50 (and_50_out, bltu, BrLt);
  not not_24 (not_24_out, BrLt);
  or or_1 (or_1_out, SB_PCsel, ImmSel[2]);
  or or_2 (ImmSel[0], MemRW, U);
  or or_3 (ImmSel[1], SB, U);
  or or_4 (ALUSel[3], mul, mulhu, lui, sub, mulh0);
  and and_51 (and_51_out, bne, not_22_out);
  and and_52 (and_52_out, bge, not_23_out);
  and and_53 (and_53_out, bge, BrEq);
  and and_54 (and_54_out, bgeu, not_24_out);
  and and_55 (and_55_out, bgeu, BrEq);
  or or_5 (ASel, BSel, I, MemRW, jalr);
  or or_6 (ALUSel[0], sra0, and0, andi, xor0, xori, srai, slt0, slti, mulhu, lui);
  or or_7 (PCSel, or_1_out, jalr);
  or or_8 (ALUSel[2], srl0, srli, sra0, srai, slli, lui, sll0, slt0, slti, sub, mulh0);
  or or_9 (BrUn, bltu, bgeu);
  not not_25 (not_25_out, MemRW);
  or or_10 (ALUSel[1], or0, ori, xor0, xori, slli, sll0, mul, slt0, slti, mulhu, mulh0);
  and and_56 (RegWEn, not_25_out, not_26_out);
  not not_26 (not_26_out, SB);
  or or_11 (SB_PCsel, and_48_out, and_51_out, and_49_out, and_52_out, and_53_out, and_50_out, and_54_out, and_55_out);
  or or_12 (WBSel[0], lb0, lh0, lw0);
  or or_13 (WBSel[1], ImmSel[2], jalr);
  or or_14 (WRITE_ENABLE[0], sb_t, sh, WRITE_ENABLE[3]);
  or or_15 (WRITE_ENABLE[1], sh, WRITE_ENABLE[3]);

  assign WRITE_ENABLE[2] = WRITE_ENABLE[3];

  // Other names for the same wires on the sheet: csr = CSRWen; csrwi = CSRSel; jal = ImmSel[2]; UJ = ImmSel[2];
  //   zero = inst[0]; one = inst[1]; two = inst[2]; three = inst[3]; four = inst[4]; five = inst[5]; six = inst[6];
  //   func3[2:0] = inst[14:12]; func7[6:0] = inst[31:25]; func7_0 = inst[25]; func7_5 = inst[30]; R = BSel; S = MemRW;
  //   sw = WRITE_ENABLE[3]

  // Notes on the sheet:
  //   INPUTS to your circuit
  //   DON'T CHANGE THE LOCATIONS OF THE INPUTS AND OUTPUTS!
  //   OUTPUT from your circuit
endmodule
