// Logisim project cpu.circ as structural Verilog: 1 circuit, main circuit cpu
module cpu (
  input  clk,
  input  [31:0] INSTRUCTION,
  input  [31:0] READ_DATA,
  output [31:0] WRITE_ADDRESS,
  output [31:0] PROGRAM_COUNTER,
  output [31:0] ra,
  output [31:0] sp,
  output [31:0] t0,
  output [31:0] t1,
  output [31:0] t2,
  output [31:0] s0,
  output [31:0] s1,
  output [31:0] a0,
  output [31:0] tohost,
  output [3:0] WRITE_ENABLE,
  output [31:0] WRITE_DATA
);

  wire A_sel, B_sel, branch_comp_1_breq, branch_comp_1_brlt, control_logic_1_brun, control_logic_1_csrwen,
       CSRSel, MenRW, PCSel, RegWEn;
  wire [1:0] WB_sel;
  wire [2:0] immsel;
  wire [3:0] ALUSel;
  wire [31:0] CSR_din, DataA, DataB, imm, INSTRUCTION_stage2, multiplexer_1_out, multiplexer_5_out,
       PROGRAM_COUNTER_plus_four, PROGRAM_COUNTER_plusfour_stage2, PROGRAM_COUNTER_stage2, read_Data1,
       write_Data_t;

  Adder #(.width(32)) adder_1 (.a(PROGRAM_COUNTER), .b(32'h4), .out(PROGRAM_COUNTER_plus_four));  // open: cin, cout
  Multiplexer #(.enable("false"), .width(32)) multiplexer_1 (
    .in0(PROGRAM_COUNTER_plus_four), .in1(WRITE_ADDRESS), .out(multiplexer_1_out), .sel(PCSel));
  Register #(.width(32)) PC (.D(multiplexer_1_out), .clk(clk), .Q(PROGRAM_COUNTER));  // open: en, clr
  Multiplexer #(.enable("false"), .width(32)) multiplexer_2 (
    .in0(PROGRAM_COUNTER_stage2), .in1(read_Data1), .out(DataA), .sel(A_sel));
  control_logic control_logic_1 (
    .CSRWen(control_logic_1_csrwen), .PCSel(PCSel), .WRITE_ENABLE(WRITE_ENABLE), .RegWEn(RegWEn),
    .ImmSel(immsel), .BrUn(control_logic_1_brun), .ASel(A_sel), .BSel(B_sel), .ALUSel(ALUSel), .MemRW(MenRW),
    .WBSel(WB_sel), .CSRSel(CSRSel), .inst(INSTRUCTION_stage2), .BrEq(branch_comp_1_breq),
    .BrLt(branch_comp_1_brlt));
  imm_gen imm_gen_1 (.inst(INSTRUCTION_stage2), .ImmSel(immsel), .imm(imm));
  Multiplexer #(.enable("false"), .width(32)) multiplexer_3 (.in0(imm), .in1(WRITE_DATA), .out(DataB), .sel(B_sel));
  regfile regfile_1 (
    .rs1(INSTRUCTION_stage2[19:15]), .rs2(INSTRUCTION_stage2[24:20]), .rd(INSTRUCTION_stage2[11:7]),
    .Write_Data(write_Data_t), .RegWEn(RegWEn), .clk(clk), .ra(ra), .sp(sp), .t0(t0), .t1(t1), .t2(t2),
    .s0(s0), .s1(s1), .a0(a0), .Read_Data_1(read_Data1), .Read_Data_2(WRITE_DATA));
  branch_comp branch_comp_1 (
    .rs1(read_Data1), .rs2(WRITE_DATA), .BrUn(control_logic_1_brun), .BrEq(branch_comp_1_breq),
    .BrLt(branch_comp_1_brlt));
  Multiplexer #(.enable("false"), .width(32)) multiplexer_4 (
    .in0(read_Data1), .in1({{27{1'b0}}, INSTRUCTION_stage2[19:15]}), .out(CSR_din), .sel(CSRSel));
  alu alu_1 (.Result(WRITE_ADDRESS), .A(DataA), .B(DataB), .ALUSel(ALUSel));
  csr csr_1 (.CSR_address(12'h51e), .CSR_din(CSR_din), .CSR_WE(control_logic_1_csrwen), .clk(clk), .tohost(tohost));
  Multiplexer #(.enable("false"), .width(32)) multiplexer_5 (
    .in0(INSTRUCTION), .in1({32{1'b0}}), .out(multiplexer_5_out), .sel(PCSel));
  Register #(.width(32)) instruction_reg (
    .D(multiplexer_5_out), .en(1'b1), .clk(clk), .Q(INSTRUCTION_stage2));  // open: clr
  Register #(.width(32)) pc_reg (.D(PROGRAM_COUNTER), .en(1'b1), .clk(clk), .Q(PROGRAM_COUNTER_stage2));  // open: clr
  Register #(.width(32)) pc_plusfour_reg (
    .D(PROGRAM_COUNTER_plus_four), .en(1'b1), .clk(clk), .Q(PROGRAM_COUNTER_plusfour_stage2));  // open: clr
  Multiplexer #(.enable("false"), .select(2), .width(32)) multiplexer_6 (
    .in0(WRITE_ADDRESS), .in1(READ_DATA), .in2(PROGRAM_COUNTER_plusfour_stage2), .out(write_Data_t),
    .sel(WB_sel));  // open: in3

  // Other names for the same wires on the sheet: rs1[4:0] = INSTRUCTION_stage2[19:15];
  //   rd[4:0] = INSTRUCTION_stage2[11:7]; rs2[4:0] = INSTRUCTION_stage2[24:20]; read_Data2[31:0] = WRITE_DATA;
  //   result[31:0] = WRITE_ADDRESS

  // Notes on the sheet:
  //   Output to IMEM
  //   A_sel
  //   IMEM (do **NOT** move this)
  //   Inputs from IMEM
  //   B_sel
  //   It is OK to move the PC, RegFile, ALU, MEM, Branch Comp, Imm Gen, and Control Logic to wherever is most convenient for you when constructing your CPU, and to delete this text
  //   Inputs/Outputs for testing. Do **NOT** move these.
  //   WB_sel
  //   Outputs To DMEM
  //   DMEM (do **NOT** move this)
  //   Inputs From DMEM
endmodule
