// Logisim project imm_gen.circ as structural Verilog: 1 circuit, main circuit imm_gen
module imm_gen (
  input  [31:0] inst,
  input  [2:0] ImmSel,
  output [31:0] imm
);

  wire [11:0] demultiplexer_1_out3, demultiplexer_1_out4;
  wire [19:0] demultiplexer_1_out0;
  wire [24:0] demultiplexer_1_out1, demultiplexer_1_out2;
  wire [31:0] imm_mid, imm_mid2;
  wire [31:1] imm_mid3, imm_mid5;
  wire [31:12] imm_mid4;

  Demultiplexer #(.enable("false"), .select(3), .width(32)) demultiplexer_1 (
    .out0({imm_mid[11:0], demultiplexer_1_out0}),
    .out1({imm_mid2[11:5], demultiplexer_1_out1[24:12], imm_mid2[4:0], demultiplexer_1_out1[6:0]}),
    .out2({imm_mid3[12], imm_mid3[10:5], demultiplexer_1_out2[24:12], imm_mid3[4:1], imm_mid3[11], demultiplexer_1_out2[6:0]}),
    .out3({imm_mid4, demultiplexer_1_out3}),
    .out4({imm_mid5[20], imm_mid5[10:1], imm_mid5[11], imm_mid5[19:12], demultiplexer_1_out4}), .in(inst),
    .sel(ImmSel));  // open: out5, out6, out7
  Shifter #(.shift("ar"), .width(20)) shifter_1 (
    .in({imm_mid[11], {19{1'b0}}}), .\dist (5'b10011), .out(imm_mid[31:12]));
  Shifter #(.shift("ar"), .width(20)) shifter_2 (
    .in({imm_mid2[11], {19{1'b0}}}), .\dist (5'b10011), .out(imm_mid2[31:12]));
  Shifter #(.shift("ar"), .width(19)) shifter_3 (
    .in({imm_mid3[12], {18{1'b0}}}), .\dist (5'b10010), .out(imm_mid3[31:13]));
  Shifter #(.shift("ar"), .width(11)) shifter_4 (
    .in({imm_mid5[20], {10{1'b0}}}), .\dist (4'b1010), .out(imm_mid5[31:21]));
  assign imm = imm_mid | imm_mid2 | {imm_mid3, 1'b0} | {imm_mid4, {12{1'b0}}} | {imm_mid5, 1'b0};  // OR_Gate or_1, 32 bits wide

  // Notes on the sheet:
  //   INPUTS to your circuit
  //   DON'T CHANGE THE LOCATIONS OF THE INPUTS AND OUTPUTS!
  //   I_type
  //   OUTPUT from your circuit
  //   S_type
  //   SB_type
  //   U_type
  //   UJ_type
endmodule
