// Logisim project regfile.circ as structural Verilog: 2 circuits, main circuit regfile
module regfile (
  input  [4:0] rs1,
  input  [4:0] rs2,
  input  [4:0] rd,
  input  [31:0] Write_Data,
  input  RegWEn,
  input  clk,
  output [31:0] ra,
  output [31:0] sp,
  output [31:0] t0,
  output [31:0] t1,
  output [31:0] t2,
  output [31:0] s0,
  output [31:0] s1,
  output [31:0] a0,
  output [31:0] Read_Data_1,
  output [31:0] Read_Data_2
);

  regs regs_1 (
    .cl(clk), .writeEnable(RegWEn), .write_data_finally(Write_Data), .rs2(rs2), .rd(rd), .rs1(rs1),
    .rd2(Read_Data_2), .rd1(Read_Data_1), .ra0(ra), .sp0(sp), .t00(t0), .t10(t1), .t20(t2), .s00(s0),
    .s10(s1), .a00(a0));

  // Other names for the same wires on the sheet: read_data1[31:0] = Read_Data_1; read_data2[31:0] = Read_Data_2;
  //   read_reg1[4:0] = rs1; read_reg2[4:0] = rs2; write_en = RegWEn; write_reg[4:0] = rd

  // Notes on the sheet:
  //   INPUTS to your circuit
  //   DON'T CHANGE THE LOCATIONS OF THE INPUTS AND OUTPUTS!
  //   These are DEBUG/TEST outputs from your circuit.
  //   OUTPUTS from your circuit
endmodule

module regs (
  input  cl,
  input  writeEnable,
  input  [31:0] write_data_finally,
  input  [4:0] rs2,
  input  [4:0] rd,
  input  [4:0] rs1,
  output [31:0] rd2,
  output [31:0] rd1,
  output [31:0] ra0,
  output [31:0] sp0,
  output [31:0] t00,
  output [31:0] t10,
  output [31:0] t20,
  output [31:0] s00,
  output [31:0] s10,
  output [31:0] a00
);

  wire we_x0, we_x1, we_x2, we_x3, we_x4, we_x5, we_x6, we_x7, we_x8, we_x9, we_x10, we_x11, we_x12, we_x13,
       we_x14, we_x15, we_x16, we_x17, we_x18, we_x19, we_x20, we_x21, we_x22, we_x23, we_x24, we_x25,
       we_x26, we_x27, we_x28, we_x29, we_x30, we_x31;
  wire [31:0] x3, x4, x11, x12, x13, x14, x15, x16, x17, x18, x19, x20, x21, x22, x23, x24, x25, x26, x27,
       x28, x29, x30, x31, x117;

  Register #(.width(32)) register_1 (.D(write_data_finally), .en(we_x24), .clk(cl), .Q(x24));  // open: clr
  Register #(.width(32)) register_2 (.D(write_data_finally), .en(we_x28), .clk(cl), .Q(x28));  // open: clr
  Register #(.width(32)) register_3 (.D(write_data_finally), .en(we_x4), .clk(cl), .Q(x4));  // open: clr
  Register #(.width(32)) register_4 (.D(write_data_finally), .en(we_x8), .clk(cl), .Q(s00));  // open: clr
  Register #(.width(32)) register_5 (.D(write_data_finally), .en(we_x12), .clk(cl), .Q(x12));  // open: clr
  Register #(.width(32)) register_6 (.D(write_data_finally), .en(we_x16), .clk(cl), .Q(x16));  // open: clr
  Register #(.width(32)) register_7 (.D(write_data_finally), .en(we_x20), .clk(cl), .Q(x20));  // open: clr
  Register #(.width(32)) register_8 (.D(write_data_finally), .en(we_x1), .clk(cl), .Q(ra0));  // open: clr
  Register #(.width(32)) register_9 (.D(write_data_finally), .en(we_x5), .clk(cl), .Q(t00));  // open: clr
  Register #(.width(32)) register_10 (.D(write_data_finally), .en(we_x9), .clk(cl), .Q(s10));  // open: clr
  Register #(.width(32)) register_11 (.D(write_data_finally), .en(we_x13), .clk(cl), .Q(x13));  // open: clr
  Register #(.width(32)) register_12 (.D(write_data_finally), .en(we_x17), .clk(cl), .Q(x117));  // open: clr
  Register #(.width(32)) register_13 (.D(write_data_finally), .en(we_x21), .clk(cl), .Q(x21));  // open: clr
  Register #(.width(32)) register_14 (.D(write_data_finally), .en(we_x25), .clk(cl), .Q(x25));  // open: clr
  Register #(.width(32)) register_15 (.D(write_data_finally), .en(we_x29), .clk(cl), .Q(x29));  // open: clr
  Register #(.width(32)) register_16 (.D(write_data_finally), .en(we_x18), .clk(cl), .Q(x18));  // open: clr
  Register #(.width(32)) register_17 (.D(write_data_finally), .en(we_x22), .clk(cl), .Q(x22));  // open: clr
  Register #(.width(32)) register_18 (.D(write_data_finally), .en(we_x26), .clk(cl), .Q(x26));  // open: clr
  Register #(.width(32)) register_19 (.D(write_data_finally), .en(we_x30), .clk(cl), .Q(x30));  // open: clr
  Register #(.width(32)) register_20 (.D(write_data_finally), .en(we_x2), .clk(cl), .Q(sp0));  // open: clr
  Register #(.width(32)) register_21 (.D(write_data_finally), .en(we_x6), .clk(cl), .Q(t10));  // open: clr
  Register #(.width(32)) register_22 (.D(write_data_finally), .en(we_x10), .clk(cl), .Q(a00));  // open: clr
  Register #(.width(32)) register_23 (.D(write_data_finally), .en(we_x14), .clk(cl), .Q(x14));  // open: clr
  Register #(.width(32)) register_24 (.D(write_data_finally), .en(we_x3), .clk(cl), .Q(x3));  // open: clr
  Register #(.width(32)) register_25 (.D(write_data_finally), .en(we_x7), .clk(cl), .Q(t20));  // open: clr
  Register #(.width(32)) register_26 (.D(write_data_finally), .en(we_x11), .clk(cl), .Q(x11));  // open: clr
  Register #(.width(32)) register_27 (.D(write_data_finally), .en(we_x15), .clk(cl), .Q(x15));  // open: clr
  Register #(.width(32)) register_28 (.D(write_data_finally), .en(we_x19), .clk(cl), .Q(x19));  // open: clr
  Register #(.width(32)) register_29 (.D(write_data_finally), .en(we_x23), .clk(cl), .Q(x23));  // open: clr
  Register #(.width(32)) register_30 (.D(write_data_finally), .en(we_x27), .clk(cl), .Q(x27));  // open: clr
  Register #(.width(32)) register_31 (.D(write_data_finally), .en(we_x31), .clk(cl), .Q(x31));  // open: clr
  Demultiplexer #(.enable("false"), .select(5)) demultiplexer_1 (
    .out0(we_x0), .out1(we_x1), .out2(we_x2), .out3(we_x3), .out4(we_x4), .out5(we_x5), .out6(we_x6),
    .out7(we_x7), .out8(we_x8), .out9(we_x9), .out10(we_x10), .out11(we_x11), .out12(we_x12), .out13(we_x13),
    .out14(we_x14), .out15(we_x15), .out16(we_x16), .out17(we_x17), .out18(we_x18), .out19(we_x19),
    .out20(we_x20), .out21(we_x21), .out22(we_x22), .out23(we_x23), .out24(we_x24), .out25(we_x25),
    .out26(we_x26), .out27(we_x27), .out28(we_x28), .out29(we_x29), .out30(we_x30), .out31(we_x31),
    .in(writeEnable), .sel(rd));
  Multiplexer #(.enable("false"), .select(5), .width(32)) multiplexer_1 (
    .in0({32{1'b0}}), .in1(ra0), .in2(sp0), .in3(x3), .in4(x4), .in5(t00), .in6(t10), .in7(t20), .in8(s00),
    .in9(s10), .in10(a00), .in11(x11), .in12(x12), .in13(x13), .in14(x14), .in15(x15), .in16(x16),
    .in17(x17), .in18(x18), .in19(x19), .in20(x20), .in21(x21), .in22(x22), .in23(x23), .in24(x24),
    .in25(x25), .in26(x26), .in27(x27), .in28(x28), .in29(x29), .in30(x30), .in31(x31), .out(rd1), .sel(rs1));
  Multiplexer #(.enable("false"), .select(5), .width(32)) multiplexer_2 (
    .in0({32{1'b0}}), .in1(ra0), .in2(sp0), .in3(x3), .in4(x4), .in5(t00), .in6(t10), .in7(t20), .in8(s00),
    .in9(s10), .in10(a00), .in11(x11), .in12(x12), .in13(x13), .in14(x14), .in15(x15), .in16(x16),
    .in17(x17), .in18(x18), .in19(x19), .in20(x20), .in21(x21), .in22(x22), .in23(x23), .in24(x24),
    .in25(x25), .in26(x26), .in27(x27), .in28(x28), .in29(x29), .in30(x30), .in31(x31), .out(rd2), .sel(rs2));

  // Other names for the same wires on the sheet: wd[31:0] = write_data_finally; we = writeEnable; x1[31:0] = ra0;
  //   x2[31:0] = sp0; x5[31:0] = t00; x6[31:0] = t10; x7[31:0] = t20; x8[31:0] = s00; x9[31:0] = s10; x10[31:0] = a00
endmodule
